# Fritzing sketch PulseSensor (saved by Fritzing 0.9.3b)

parts:
  Часть1 = Arduino Uno (Rev3)
  PS = LM35 Temperature Sensor [package="TO92 [THT]"]

nets:
  N1: Часть1.A0, PS.+Vs
  GND: Часть1.GND, PS.GND
  N2: Часть1.5V, PS.Vout
